# Fritzing sketch lcd-touch (saved by Fritzing 0.9.3b)
breadboards: 1

parts:
  Part1 = Arduino Uno (Rev3)
  LCD1 = LCD screen
  R1 = Resistor [tolerance=±5% resistance=560 package=THT]
  U1 = TRANSISTOR_NPN_2 [package=to-92]
  Part2 = MPR121 Breakout
  R2 = Resistor [tolerance=±5% resistance=2.2k package=THT]
  R3 = Resistor [tolerance=±5% resistance=2.2k package=THT]
  OMRON2 = OMRON PCB Power Relay – G5LE [part_number="G5LE-1\n" package=THT]
  U2 = LTC3105 [package=msop-12]
  L1 = Solenoid

nets:
  N1: Part1.A4/SDA, Part2.SDA, R3.Pin_1
  N2: Part1.A5/SCL, Part2.SCL
  N3: Part1.D11_PWM/MOSI, LCD1.E
  N4: Part1.D12/MISO, LCD1.RS
  N5: Part1.D13/SCK, OMRON2.IN
  N6: Part1.D2, LCD1.DB7
  N7: Part1.D3_PWM, LCD1.DB6
  N8: Part1.D4, LCD1.DB5
  N9: Part1.D5_PWM, LCD1.DB4
  N10: Part1.D6_PWM, U1.B
  N11: Part1.D7, Part2.~IRQ
  3V3: Part1.3V3, Part2.3.3V
  5V: Part1.5V, LCD1.VDD, OMRON2.VCC, U2.VIN, L1.pin1
  GND: Part1.GND, LCD1.VSS, LCD1.V0, LCD1.R/W, R1.Pin_0, U1.E, Part2.GND, R2.Pin_0, R3.Pin_0
  N12: LCD1.LED+, R1.Pin_1
  N13: LCD1.LED-, U1.C
  N14: OMRON2.COM, U2.VOUT
  N15: OMRON2.NO, L1.pin2

custom parts:
  OMRON PCB Power Relay – G5LE: A Cubic, Single-pole 10-A Power Relay - ROHS compliant - Sub-miniature ‘sugar cube’ relay with universal terminal footprint - Conforms to EN 61810-1, UL508, CSA22.2 - Tracking resistance: CTI>250 (-VD type) - UL class-F coil insulation model available (UL class-B coil insulation for standard model) - High switching power: 10 A - Two types of seal available; flux protection and fully sealed -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
